# Fritzing sketch KeyboardFritzingCircuit (saved by Fritzing 0.9.3b)
breadboards: 1

parts:
  Part1 = Adafruit Feather nRF52 [part_number="Adafruit #3406"]
  R1 = Resistor [tolerance=±5% resistance=10k package="0805 [SMD]"]
  R3 = Resistor [tolerance=±5% resistance=10k package="0805 [SMD]"]
  R4 = Resistor [tolerance=±5% resistance=10k package="0805 [SMD]"]
  U1 = POT_SWITCH [package=pot_pth_switch]
  TRRS1 = Audio Jack (TRRS) 3.5mm [part_number="LUMBERG JEITA RC-5325A" package="RC-5325A [SMD]"]
  TRRS2 = Audio Jack (TRRS) 3.5mm [part_number="LUMBERG JEITA RC-5325A" package="RC-5325A [SMD]"]
  TRRS3 = Audio Jack (TRRS) 3.5mm [part_number="LUMBERG JEITA RC-5325A" package="RC-5325A [SMD]"]

nets:
  N1: Part1.3.3V, U1.G$1_A, TRRS1.TIP, TRRS2.TIP, TRRS3.SLEEVE
  N2: Part1.GND, R1.Pin_1, R3.Pin_1, R4.Pin_0, U1.G$2_2
  N3: Part1.A1/0.03, R3.Pin_0, TRRS2.SLEEVE
  N4: Part1.A2/0.04, U1.G$2_1
  N5: Part1.EN, U1.G$1_S
  N6: R4.Pin_1, TRRS3.TIP
